# Fritzing sketch 03_spinMotorSpin (saved by Fritzing 0.9.0b)
breadboards: 1

parts:
  Part1 = Arduino Uno (Rev3)
  Q1 = NPN-Transistor [package="TO92 [THT]"]
  R1 = Resistor [tolerance=±5% resistance=2.2k package=THT]
  M2 = DC Motor
  D1 = Diode [package=diode-1n4001]

nets:
  N1: Part1.D9_PWM, R1.Pin_1
  N2: Part1.5V, M2.pin_2, D1.C
  N3: Part1.GND, Q1.E
  N4: Q1.B, R1.Pin_0
  N5: Q1.C, M2.pin_1, D1.A
